// Logisim project me6_Mendaros_J.circ as structural Verilog: 5 circuits, main circuit MIPS
module MIPS (
  input  in_1,
  input  rst
);

  wire and_1_out, and_2_out, bitwise_imm, clk, comparator_1_eq, comparator_2_eq, comparator_3_eq,
       comparator_4_eq, comparator_5_eq, comparator_6_eq, comparator_7_eq, comparator_8_eq, comparator_9_eq,
       comparator_10_eq, comparator_11_eq, comparator_12_eq, comparator_13_eq, comparator_14_eq,
       comparator_15_eq, is_itype, multiplexer_3_out, multiplexer_8_out, or_2_out, or_5_out, wr_en;
  wire [4:0] _16_20, inst_mem_1_inst_3, multiplexer_4_out;
  wire [5:0] _31_26, ALU_code;
  wire [15:0] inst_mem_1_inst_2;
  wire [25:21] inst_mem_1_inst;
  wire [31:0] adder_1_out, adder_2_out, alu_res, bit_extender_1_out, data_mem_1_data_out, imm_1, imm_final,
       multiplexer_5_out, multiplexer_6_out, multiplexer_7_out, PC, reg_file_1_rd_data1, reg_file_1_rd_data2,
       shifter_1_out;

  Clock u_clk (.out(clk));
  Register #(.width(32)) u_PC (.D(multiplexer_6_out), .en(1'b1), .Q(PC), .clk(clk), .clr(rst));
  assign bit_extender_1_out = {{16{1'b0}}, {inst_mem_1_inst_2[15:11], inst_mem_1_inst_3, inst_mem_1_inst_2[5:0]}};  // Bit_Extender bit_extender_1
  Adder #(.width(32)) adder_1 (.a(32'h4), .b(PC), .out(adder_1_out));  // open: cin, cout
  Multiplexer #(.width(32), .enable("false")) multiplexer_1 (
    .in0(imm_1), .in1(bit_extender_1_out), .out(imm_final), .sel(bitwise_imm));
  // Probe on PC
  // Probe on {_31_26, inst_mem_1_inst, _16_20, inst_mem_1_inst_2[15:11], inst_mem_1_inst_3, inst_mem_1_inst_2[5:0]}
  // Probe on inst_mem_1_inst_2[5:0]
  INST_MEM inst_mem_1 (
    .inst_addr(PC),
    .inst({_31_26, inst_mem_1_inst, _16_20, inst_mem_1_inst_2[15:11], inst_mem_1_inst_3, inst_mem_1_inst_2[5:0]}));
  // Probe on _31_26
  // Probe on inst_mem_1_inst_2[5:0]
  // Probe on inst_mem_1_inst_2[5:0]
  Multiplexer #(.width(6), .enable("false")) multiplexer_2 (
    .in0(_31_26), .in1(inst_mem_1_inst_2[5:0]), .out(ALU_code), .sel(comparator_1_eq));
  Comparator #(.width(6)) comparator_1 (.a(_31_26), .b({6{1'b0}}), .eq(comparator_1_eq));  // open: gt, lt
  Multiplexer #(.enable("false")) multiplexer_3 (.in0(1'b1), .in1(1'b0), .out(multiplexer_3_out), .sel(wr_en));
  Multiplexer #(.width(5), .enable("false")) multiplexer_4 (
    .in0(_16_20), .in1(inst_mem_1_inst_2[15:11]), .out(multiplexer_4_out), .sel(comparator_1_eq));
  assign imm_1 = {{16{inst_mem_1_inst_2[15]}}, {inst_mem_1_inst_2[15:11], inst_mem_1_inst_3, inst_mem_1_inst_2[5:0]}};  // Bit_Extender bit_extender_2
  Comparator #(.width(6)) comparator_2 (.a(_31_26), .b(6'b101011), .eq(comparator_2_eq));  // open: gt, lt
  Comparator #(.width(6)) comparator_3 (.a(_31_26), .b(6'b000101), .eq(comparator_3_eq));  // open: gt, lt
  Comparator #(.width(6)) comparator_4 (.a(_31_26), .b(6'b000100), .eq(comparator_4_eq));  // open: gt, lt
  // Probe on multiplexer_3_out
  or or_1 (wr_en, comparator_2_eq, comparator_3_eq, comparator_4_eq);
  // Probe on adder_1_out
  // Probe on imm_1
  REG_FILE reg_file_1 (
    .wr_data(multiplexer_7_out), .clk(clk), .rst(rst), .wr_en(multiplexer_3_out), .wr_reg(multiplexer_4_out),
    .rd_data1(reg_file_1_rd_data1), .rd_data2(reg_file_1_rd_data2), .rd_reg1(inst_mem_1_inst),
    .rd_reg2(_16_20));
  Comparator #(.width(6)) comparator_5 (.a(_31_26), .b(6'b100011), .eq(comparator_5_eq));  // open: gt, lt
  or or_2 (or_2_out, comparator_5_eq, comparator_6_eq);
  Comparator #(.width(6)) comparator_6 (.a(_31_26), .b(6'b101011), .eq(comparator_6_eq));  // open: gt, lt
  Comparator #(.width(6)) comparator_7 (.a(_31_26), .b(6'b001100), .eq(comparator_7_eq));  // open: gt, lt
  or or_3 (bitwise_imm, comparator_7_eq, comparator_8_eq, comparator_9_eq);
  Comparator #(.width(6)) comparator_8 (.a(_31_26), .b(6'b001101), .eq(comparator_8_eq));  // open: gt, lt
  Comparator #(.width(6)) comparator_9 (.a(_31_26), .b(6'b001110), .eq(comparator_9_eq));  // open: gt, lt
  // Probe on reg_file_1_rd_data2
  // Probe on multiplexer_5_out
  Multiplexer #(.width(32), .enable("false")) multiplexer_5 (
    .in0(reg_file_1_rd_data2), .in1(imm_final), .out(multiplexer_5_out), .sel(is_itype));
  or or_4 (is_itype, or_2_out, bitwise_imm);
  // Probe on ALU_code
  Shifter #(.width(32)) shifter_1 (.in(imm_1), .\dist (5'b00010), .out(shifter_1_out));
  // Probe on shifter_1_out
  // Probe on reg_file_1_rd_data1
  // Probe on imm_1
  // Probe on ALU_code
  // Probe on inst_mem_1_inst_3
  // Probe on multiplexer_6_out
  Multiplexer #(.width(32), .enable("false")) multiplexer_6 (
    .in0(adder_1_out), .in1(adder_2_out), .out(multiplexer_6_out), .sel(or_5_out));
  Adder #(.width(32)) adder_2 (.a(adder_1_out), .b(shifter_1_out), .out(adder_2_out));  // open: cin, cout
  // Probe on adder_2_out
  // Probe on or_5_out
  // Probe on multiplexer_7_out
  // Probe on ALU_code
  // Probe on alu_res
  // Probe on _31_26
  ALU alu_1 (
    .imm(imm_1), .shamt(inst_mem_1_inst_3), .op1(reg_file_1_rd_data1), .op2(multiplexer_5_out),
    .result(alu_res), .ALU_code(ALU_code));
  Multiplexer #(.width(32), .enable("false")) multiplexer_7 (
    .in0(alu_res), .in1(data_mem_1_data_out), .out(multiplexer_7_out), .sel(comparator_10_eq));
  Comparator #(.width(6)) comparator_10 (.a(6'b100011), .b(ALU_code), .eq(comparator_10_eq));  // open: gt, lt
  // Probe on comparator_10_eq
  Comparator #(.width(6)) comparator_11 (.a(ALU_code), .b(6'b000100), .eq(comparator_11_eq));  // open: gt, lt
  Comparator #(.width(32)) comparator_12 (.a(alu_res), .b(32'h1), .eq(comparator_12_eq));  // open: gt, lt
  Comparator #(.width(6)) comparator_13 (.a(ALU_code), .b(6'b000101), .eq(comparator_13_eq));  // open: gt, lt
  Comparator #(.width(32)) comparator_14 (.a(alu_res), .b({32{1'b1}}), .eq(comparator_14_eq));  // open: gt, lt
  Comparator #(.width(6)) comparator_15 (.a(6'b101011), .b(ALU_code), .eq(comparator_15_eq));  // open: gt, lt
  and and_1 (and_1_out, comparator_11_eq, comparator_12_eq);
  and and_2 (and_2_out, comparator_13_eq, comparator_14_eq);
  // Probe on multiplexer_8_out
  Multiplexer #(.enable("false")) multiplexer_8 (
    .in0(1'b0), .in1(1'b1), .out(multiplexer_8_out), .sel(comparator_15_eq));
  // Probe on comparator_15_eq
  DATA_MEM data_mem_1 (
    .addr(alu_res), .data_in(reg_file_1_rd_data2), .data_out(data_mem_1_data_out), .store(multiplexer_8_out),
    .clk(clk), .rst(rst));
  // Probe on data_mem_1_data_out
  or or_5 (or_5_out, and_1_out, and_2_out);

  // Notes on the sheet:
  //   sw
  //   bne
  //   beq
  //   sw
  //   rs
  //   rt
  //   rd
  //   sel_dest
  //   address
  //   sw
  //   andi
  //   ori
  //   lw
  //   xori
  //   sel_opB
  //   PC+4
  //   branch target
  //   sel_pc
  //   sel_data
  //   beq
  //   bne
  //   mem_wr
endmodule

module DATA_MEM (
  input  [31:0] addr,
  input  [31:0] data_in,
  input  store,
  input  clk,
  input  rst,
  output [31:0] data_out
);

  RAM #(.dataWidth(32), .bus("separate")) ram_1 (
    .addr(addr[9:2]), .din(data_in), .data(data_out), .str(store), .sel(1'b1), .clk(clk), .ld(1'b1), .clr(rst));
endmodule

module INST_MEM (
  input  [31:0] inst_addr,
  output [31:0] inst
);

  wire [31:0] rom_1_data, rom_2_data;

  ROM #(.addrWidth(13), .dataWidth(32)) rom_1 (.addr(inst_addr[14:2]), .data(rom_1_data), .sel(1'b1));
  ROM #(.addrWidth(13), .dataWidth(32)) rom_2 (.addr(inst_addr[14:2]), .data(rom_2_data), .sel(1'b1));
  Multiplexer #(.width(32), .enable("false")) multiplexer_1 (
    .in0(rom_1_data), .in1(rom_2_data), .out(inst), .sel(inst_addr[15]));

  // Notes on the sheet:
  //   Main INST_MEM (0x0000-0x7FFC)
  //   ISR INST_MEM (0xF000-0xFFFC)
  //   contents of rom_1 (hex, n*v repeats v):
  //   c63022 e73822 1084022 1294822 20060005 20070010 20080015 20090020 14a5022 201f1001 8fea0000 afe60010
  //   afe70014 afe80018 afe9001c 20010004 20020004 30450004 34460000 38470000
endmodule

module REG_FILE (
  input  [31:0] wr_data,
  input  clk,
  input  rst,
  input  [4:0] rd_reg1,
  input  wr_en,
  input  [4:0] wr_reg,
  input  [4:0] rd_reg2,
  output [31:0] rd_data1,
  output [31:0] rd_data2
);

  wire W00, W01, W02, W03, W04, W05, W06, W07, W08, W09, W10, W11, W12, W13, W14, W15, W16, W17, W18, W19,
       W20, W21, W22, W23, W24, W25, W26, W27, W28, W29, W30, W31;
  wire [31:0] Q01, Q02, Q03, Q04, Q05, Q06, Q07, Q08, Q09, Q10, Q11, Q12, Q13, Q14, Q15, Q16, Q17, Q18, Q19,
       Q20, Q21, Q22, Q23, Q24, Q25, Q26, Q27, Q28, Q29, Q30, Q31;

  Demultiplexer #(.select(5), .disabled(0)) demultiplexer_1 (
    .out0(W00), .out1(W01), .out2(W02), .out3(W03), .out4(W04), .out5(W05), .out6(W06), .out7(W07),
    .out8(W08), .out9(W09), .out10(W10), .out11(W11), .out12(W12), .out13(W13), .out14(W14), .out15(W15),
    .out16(W16), .out17(W17), .out18(W18), .out19(W19), .out20(W20), .out21(W21), .out22(W22), .out23(W23),
    .out24(W24), .out25(W25), .out26(W26), .out27(W27), .out28(W28), .out29(W29), .out30(W30), .out31(W31),
    .in(1'b1), .sel(wr_reg), .en(wr_en));
  Register #(.width(32)) register_1 (.D(wr_data), .en(W01), .Q(Q01), .clk(clk), .clr(rst));
  Register #(.width(32)) register_2 (.D(wr_data), .en(W02), .Q(Q02), .clk(clk), .clr(rst));
  Register #(.width(32)) register_3 (.D(wr_data), .en(W03), .Q(Q03), .clk(clk), .clr(rst));
  Register #(.width(32)) register_4 (.D(wr_data), .en(W04), .Q(Q04), .clk(clk), .clr(rst));
  Register #(.width(32)) register_5 (.D(wr_data), .en(W05), .Q(Q05), .clk(clk), .clr(rst));
  Register #(.width(32)) register_6 (.D(wr_data), .en(W06), .Q(Q06), .clk(clk), .clr(rst));
  Register #(.width(32)) register_7 (.D(wr_data), .en(W07), .Q(Q07), .clk(clk), .clr(rst));
  // Probe on {32{1'b0}}
  // Probe on Q01
  // Probe on Q02
  // Probe on Q03
  // Probe on Q04
  // Probe on Q05
  // Probe on Q06
  // Probe on Q07
  // Probe on Q08
  // Probe on Q09
  // Probe on Q10
  // Probe on Q11
  // Probe on Q12
  // Probe on Q13
  // Probe on Q14
  // Probe on Q15
  Register #(.width(32)) register_8 (.D(wr_data), .en(W08), .Q(Q08), .clk(clk), .clr(rst));
  Register #(.width(32)) register_9 (.D(wr_data), .en(W09), .Q(Q09), .clk(clk), .clr(rst));
  Register #(.width(32)) register_10 (.D(wr_data), .en(W10), .Q(Q10), .clk(clk), .clr(rst));
  Register #(.width(32)) register_11 (.D(wr_data), .en(W11), .Q(Q11), .clk(clk), .clr(rst));
  Register #(.width(32)) register_12 (.D(wr_data), .en(W12), .Q(Q12), .clk(clk), .clr(rst));
  Register #(.width(32)) register_13 (.D(wr_data), .en(W13), .Q(Q13), .clk(clk), .clr(rst));
  Register #(.width(32)) register_14 (.D(wr_data), .en(W14), .Q(Q14), .clk(clk), .clr(rst));
  Register #(.width(32)) register_15 (.D(wr_data), .en(W15), .Q(Q15), .clk(clk), .clr(rst));
  // Probe on Q16
  // Probe on Q17
  // Probe on Q18
  // Probe on Q19
  // Probe on Q20
  // Probe on Q21
  // Probe on Q22
  // Probe on Q23
  // Probe on Q24
  // Probe on Q25
  // Probe on Q26
  // Probe on Q27
  // Probe on Q28
  // Probe on Q29
  // Probe on Q30
  // Probe on Q31
  Register #(.width(32)) register_16 (.D(wr_data), .en(W16), .Q(Q16), .clk(clk), .clr(rst));
  Register #(.width(32)) register_17 (.D(wr_data), .en(W17), .Q(Q17), .clk(clk), .clr(rst));
  Register #(.width(32)) register_18 (.D(wr_data), .en(W18), .Q(Q18), .clk(clk), .clr(rst));
  Register #(.width(32)) register_19 (.D(wr_data), .en(W19), .Q(Q19), .clk(clk), .clr(rst));
  Register #(.width(32)) register_20 (.D(wr_data), .en(W20), .Q(Q20), .clk(clk), .clr(rst));
  Register #(.width(32)) register_21 (.D(wr_data), .en(W21), .Q(Q21), .clk(clk), .clr(rst));
  Register #(.width(32)) register_22 (.D(wr_data), .en(W22), .Q(Q22), .clk(clk), .clr(rst));
  Register #(.width(32)) register_23 (.D(wr_data), .en(W23), .Q(Q23), .clk(clk), .clr(rst));
  Register #(.width(32)) register_24 (.D(wr_data), .en(W24), .Q(Q24), .clk(clk), .clr(rst));
  Register #(.width(32)) register_25 (.D(wr_data), .en(W25), .Q(Q25), .clk(clk), .clr(rst));
  Register #(.width(32)) register_26 (.D(wr_data), .en(W26), .Q(Q26), .clk(clk), .clr(rst));
  Register #(.width(32)) register_27 (.D(wr_data), .en(W27), .Q(Q27), .clk(clk), .clr(rst));
  Register #(.width(32)) register_28 (.D(wr_data), .en(W28), .Q(Q28), .clk(clk), .clr(rst));
  Register #(.width(32)) register_29 (.D(wr_data), .en(W29), .Q(Q29), .clk(clk), .clr(rst));
  Register #(.width(32)) register_30 (.D(wr_data), .en(W30), .Q(Q30), .clk(clk), .clr(rst));
  Register #(.width(32)) register_31 (.D(wr_data), .en(W31), .Q(Q31), .clk(clk), .clr(rst));
  Multiplexer #(.select(5), .width(32), .disabled(0), .enable("false")) multiplexer_1 (
    .in0({32{1'b0}}), .in1(Q01), .in2(Q02), .in3(Q03), .in4(Q04), .in5(Q05), .in6(Q06), .in7(Q07), .in8(Q08),
    .in9(Q09), .in10(Q10), .in11(Q11), .in12(Q12), .in13(Q13), .in14(Q14), .in15(Q15), .in16(Q16),
    .in17(Q17), .in18(Q18), .in19(Q19), .in20(Q20), .in21(Q21), .in22(Q22), .in23(Q23), .in24(Q24),
    .in25(Q25), .in26(Q26), .in27(Q27), .in28(Q28), .in29(Q29), .in30(Q30), .in31(Q31), .out(rd_data1),
    .sel(rd_reg1));
  Multiplexer #(.select(5), .width(32), .disabled(0), .enable("false")) multiplexer_2 (
    .in0({32{1'b0}}), .in1(Q01), .in2(Q02), .in3(Q03), .in4(Q04), .in5(Q05), .in6(Q06), .in7(Q07), .in8(Q08),
    .in9(Q09), .in10(Q10), .in11(Q11), .in12(Q12), .in13(Q13), .in14(Q14), .in15(Q15), .in16(Q16),
    .in17(Q17), .in18(Q18), .in19(Q19), .in20(Q20), .in21(Q21), .in22(Q22), .in23(Q23), .in24(Q24),
    .in25(Q25), .in26(Q26), .in27(Q27), .in28(Q28), .in29(Q29), .in30(Q30), .in31(Q31), .out(rd_data2),
    .sel(rd_reg2));

  // Other names for the same wires on the sheet: D[31:0] = wr_data

  // Notes on the sheet:
  //   Write Register Select
  //   Data Input
  //   Probes of all registers (for easy debugging)
  //   Read Register Select
endmodule

module ALU (
  input  [31:0] imm,
  input  [4:0] shamt,
  input  [31:0] op1,
  input  [31:0] op2,
  input  [5:0] ALU_code,
  output [31:0] result
);

  wire comparator_1_lt, comparator_2_lt, comparator_3_eq, comparator_4_gt, comparator_4_lt, funct_add,
       funct_addi, funct_and, funct_andi, funct_beq, funct_bne, funct_lw, funct_nor, funct_or, funct_ori,
       funct_sel_en, funct_sll, funct_sllv, funct_slt, funct_slti, funct_srl, funct_srlv, funct_sub,
       funct_sw, funct_xor, funct_xori, or_3_out, or_4_out, or_5_out;
  wire [4:0] funct_sel;
  wire [31:0] res_add, res_addi, res_and, res_andi, res_beq, res_bne, res_nor, res_or, res_ori, res_sll,
       res_sllv, res_slt, res_slti, res_srl, res_srlv, res_sub, res_xor, res_xori, subtractor_2_out,
       subtractor_3_out;

  Adder #(.width(32)) adder_1 (.a(op1), .b(op2), .out(res_add));  // open: cin, cout
  Subtractor #(.width(32)) subtractor_1 (.a(op1), .b(op2), .out(res_sub));  // open: bin, bout
  assign res_and = op1 & op2;  // AND_Gate and_1, 32 bits wide
  assign res_or = op1 | op2;  // OR_Gate or_1, 32 bits wide
  assign res_nor = ~(op1 | op2);  // NOR_Gate nor_1, 32 bits wide
  assign res_xor = op1 ^ op2;  // XOR_Gate xor_1, 32 bits wide
  Adder #(.width(32)) adder_2 (.a(op1), .b(imm), .out(res_addi));  // open: cin, cout
  assign res_andi = op1 & imm;  // AND_Gate and_2, 32 bits wide
  assign res_ori = op1 | imm;  // OR_Gate or_2, 32 bits wide
  Shifter #(.width(32)) shifter_1 (.in(op2), .\dist (shamt), .out(res_sll));
  Shifter #(.width(32), .shift("lr")) shifter_2 (.in(op2), .\dist (shamt), .out(res_srl));
  assign res_xori = op1 ^ imm;  // XOR_Gate xor_2, 32 bits wide
  Comparator #(.width(32)) comparator_1 (.a(op1), .b(op2), .lt(comparator_1_lt));  // open: gt, eq
  Comparator #(.width(32)) comparator_2 (.a(op1), .b(imm), .lt(comparator_2_lt));  // open: gt, eq
  Subtractor #(.width(32)) subtractor_2 (.a(op1), .b(op2), .out(subtractor_2_out));  // open: bin, bout
  // Probe on subtractor_3_out
  Subtractor #(.width(32)) subtractor_3 (.a(op1), .b(op2), .out(subtractor_3_out));  // open: bin, bout
  // Probe on op1[4:0]
  assign res_slt = {{31{1'b0}}, or_3_out};  // Bit_Extender bit_extender_1
  or or_3 (or_3_out, comparator_1_lt, 1'b0);
  assign res_slti = {{31{1'b0}}, or_4_out};  // Bit_Extender bit_extender_2
  or or_4 (or_4_out, comparator_2_lt, 1'b0);
  // Probe on comparator_3_eq
  Comparator #(.width(32)) comparator_3 (.a(subtractor_2_out), .b({32{1'b0}}), .eq(comparator_3_eq));  // open: gt, lt
  Comparator #(.width(32)) comparator_4 (
    .a(subtractor_3_out), .b({32{1'b0}}), .gt(comparator_4_gt), .lt(comparator_4_lt));  // open: eq
  or or_5 (or_5_out, comparator_4_gt, comparator_4_lt);
  // Probe on res_add
  // Probe on res_sub
  // Probe on res_addi
  // Probe on op1
  assign res_beq = {{31{1'b0}}, comparator_3_eq};  // Bit_Extender bit_extender_3
  // Probe on or_5_out
  assign res_bne = {{31{or_5_out}}, or_5_out};  // Bit_Extender bit_extender_4
  // Probe on op2
  Shifter #(.width(32)) shifter_3 (.in(op2), .\dist (op1[4:0]), .out(res_sllv));
  Shifter #(.width(32), .shift("lr")) shifter_4 (.in(op2), .\dist (op1[4:0]), .out(res_srlv));
  // Probe on op2
  // Probe on res_sllv
  Comparator #(.width(6)) comparator_5 (.a(ALU_code), .b(6'b100000), .eq(funct_add));  // open: gt, lt
  Comparator #(.width(6)) comparator_6 (.a(ALU_code), .b(6'b100010), .eq(funct_sub));  // open: gt, lt
  Comparator #(.width(6)) comparator_7 (.a(ALU_code), .b(6'b100100), .eq(funct_and));  // open: gt, lt
  Comparator #(.width(6)) comparator_8 (.a(ALU_code), .b(6'b100101), .eq(funct_or));  // open: gt, lt
  Comparator #(.width(6)) comparator_9 (.a(ALU_code), .b(6'b100111), .eq(funct_nor));  // open: gt, lt
  Comparator #(.width(6)) comparator_10 (.a(ALU_code), .b(6'b100110), .eq(funct_xor));  // open: gt, lt
  Comparator #(.width(6)) comparator_11 (.a(ALU_code), .b(6'b101010), .eq(funct_slt));  // open: gt, lt
  Comparator #(.width(6)) comparator_12 (.a(ALU_code), .b({6{1'b0}}), .eq(funct_sll));  // open: gt, lt
  Comparator #(.width(6)) comparator_13 (.a(ALU_code), .b(6'b000010), .eq(funct_srl));  // open: gt, lt
  Comparator #(.width(6)) comparator_14 (.a(ALU_code), .b(6'b001000), .eq(funct_addi));  // open: gt, lt
  Comparator #(.width(6)) comparator_15 (.a(ALU_code), .b(6'b001010), .eq(funct_slti));  // open: gt, lt
  Comparator #(.width(6)) comparator_16 (.a(ALU_code), .b(6'b001100), .eq(funct_andi));  // open: gt, lt
  Comparator #(.width(6)) comparator_17 (.a(ALU_code), .b(6'b001101), .eq(funct_ori));  // open: gt, lt
  Comparator #(.width(6)) comparator_18 (.a(ALU_code), .b(6'b001110), .eq(funct_xori));  // open: gt, lt
  Comparator #(.width(6)) comparator_19 (.a(ALU_code), .b(6'b000100), .eq(funct_beq));  // open: gt, lt
  Comparator #(.width(6)) comparator_20 (.a(ALU_code), .b(6'b000101), .eq(funct_bne));  // open: gt, lt
  Comparator #(.width(6)) comparator_21 (.a(ALU_code), .b(6'b101011), .eq(funct_sw));  // open: gt, lt
  Comparator #(.width(6)) comparator_22 (.a(ALU_code), .b(6'b100011), .eq(funct_lw));  // open: gt, lt
  Comparator #(.width(6)) comparator_23 (.a(ALU_code), .b(6'b000110), .eq(funct_srlv));  // open: gt, lt
  Comparator #(.width(6)) comparator_24 (.a(ALU_code), .b(6'b000100), .eq(funct_sllv));  // open: gt, lt
  Multiplexer #(.select(5), .width(32)) multiplexer_1 (
    .in0(res_add), .in1(res_sub), .in2(res_and), .in3(res_or), .in4(res_nor), .in5(res_xor), .in6(res_slt),
    .in7(res_sll), .in8(res_srl), .in9(res_addi), .in10(res_slti), .in11(res_andi), .in12(res_ori),
    .in13(res_xori), .in14(res_beq), .in15(res_bne), .in16(res_add), .in17(res_add), .in18(res_srlv),
    .in19(res_sllv), .out(result), .sel(funct_sel), .en(funct_sel_en));  // open: in20, in21, in22, in23, in24, in25, in26, in27, in28, in29, in30, in31
  Priority_Encoder #(.select(5)) priority_encoder_1 (
    .in0(funct_add), .in1(funct_sub), .in2(funct_and), .in3(funct_or), .in4(funct_nor), .in5(funct_xor),
    .in6(funct_slt), .in7(funct_sll), .in8(funct_srl), .in9(funct_addi), .in10(funct_slti),
    .in11(funct_andi), .in12(funct_ori), .in13(funct_xori), .in14(funct_beq), .in15(funct_bne),
    .in16(funct_sw), .in17(funct_lw), .in18(funct_srlv), .in19(funct_sllv), .out(funct_sel),
    .gs(funct_sel_en), .en_in(1'b1));  // open: in20, in21, in22, in23, in24, in25, in26, in27, in28, in29, in30, in31, en_out

  // Other names for the same wires on the sheet: res_lw[31:0] = res_add; res_sw[31:0] = res_add

  // Notes on the sheet:
  //   Results 
endmodule
