// Logisim project me6_library.circ as structural Verilog: 4 circuits, main circuit DATA_MEM
module DATA_MEM (
  input  [31:0] addr,
  input  [31:0] data_in,
  input  store,
  input  clk,
  input  rst,
  output [31:0] data_out
);

  RAM #(.dataWidth(32), .bus("separate")) ram_1 (
    .addr(addr[9:2]), .din(data_in), .data(data_out), .str(store), .sel(1'b1), .clk(clk), .ld(1'b1), .clr(rst));
endmodule

module INST_MEM (
  input  [31:0] inst_addr,
  output [31:0] inst
);

  wire [31:0] rom_1_data, rom_2_data;

  ROM #(.addrWidth(13), .dataWidth(32)) rom_1 (.addr(inst_addr[14:2]), .data(rom_1_data), .sel(1'b1));
  ROM #(.addrWidth(13), .dataWidth(32)) rom_2 (.addr(inst_addr[14:2]), .data(rom_2_data), .sel(1'b1));
  Multiplexer #(.width(32), .enable("false")) multiplexer_1 (
    .in0(rom_1_data), .in1(rom_2_data), .out(inst), .sel(inst_addr[15]));

  // Notes on the sheet:
  //   Main INST_MEM (0x0000-0x7FFC)
  //   ISR INST_MEM (0xF000-0xFFFC)
endmodule

module REG_FILE (
  input  [31:0] wr_data,
  input  clk,
  input  rst,
  input  [4:0] rd_reg1,
  input  wr_en,
  input  [4:0] wr_reg,
  input  [4:0] rd_reg2,
  output [31:0] rd_data1,
  output [31:0] rd_data2
);

  wire W00, W01, W02, W03, W04, W05, W06, W07, W08, W09, W10, W11, W12, W13, W14, W15, W16, W17, W18, W19,
       W20, W21, W22, W23, W24, W25, W26, W27, W28, W29, W30, W31;
  wire [31:0] Q01, Q02, Q03, Q04, Q05, Q06, Q07, Q08, Q09, Q10, Q11, Q12, Q13, Q14, Q15, Q16, Q17, Q18, Q19,
       Q20, Q21, Q22, Q23, Q24, Q25, Q26, Q27, Q28, Q29, Q30, Q31;

  Demultiplexer #(.select(5), .disabled(0)) demultiplexer_1 (
    .out0(W00), .out1(W01), .out2(W02), .out3(W03), .out4(W04), .out5(W05), .out6(W06), .out7(W07),
    .out8(W08), .out9(W09), .out10(W10), .out11(W11), .out12(W12), .out13(W13), .out14(W14), .out15(W15),
    .out16(W16), .out17(W17), .out18(W18), .out19(W19), .out20(W20), .out21(W21), .out22(W22), .out23(W23),
    .out24(W24), .out25(W25), .out26(W26), .out27(W27), .out28(W28), .out29(W29), .out30(W30), .out31(W31),
    .in(1'b1), .sel(wr_reg), .en(wr_en));
  Register #(.width(32)) register_1 (.D(wr_data), .en(W01), .Q(Q01), .clk(clk), .clr(rst));
  Register #(.width(32)) register_2 (.D(wr_data), .en(W02), .Q(Q02), .clk(clk), .clr(rst));
  Register #(.width(32)) register_3 (.D(wr_data), .en(W03), .Q(Q03), .clk(clk), .clr(rst));
  Register #(.width(32)) register_4 (.D(wr_data), .en(W04), .Q(Q04), .clk(clk), .clr(rst));
  Register #(.width(32)) register_5 (.D(wr_data), .en(W05), .Q(Q05), .clk(clk), .clr(rst));
  Register #(.width(32)) register_6 (.D(wr_data), .en(W06), .Q(Q06), .clk(clk), .clr(rst));
  Register #(.width(32)) register_7 (.D(wr_data), .en(W07), .Q(Q07), .clk(clk), .clr(rst));
  // Probe on {32{1'b0}}
  // Probe on Q01
  // Probe on Q02
  // Probe on Q03
  // Probe on Q04
  // Probe on Q05
  // Probe on Q06
  // Probe on Q07
  // Probe on Q08
  // Probe on Q09
  // Probe on Q10
  // Probe on Q11
  // Probe on Q12
  // Probe on Q13
  // Probe on Q14
  // Probe on Q15
  Register #(.width(32)) register_8 (.D(wr_data), .en(W08), .Q(Q08), .clk(clk), .clr(rst));
  Register #(.width(32)) register_9 (.D(wr_data), .en(W09), .Q(Q09), .clk(clk), .clr(rst));
  Register #(.width(32)) register_10 (.D(wr_data), .en(W10), .Q(Q10), .clk(clk), .clr(rst));
  Register #(.width(32)) register_11 (.D(wr_data), .en(W11), .Q(Q11), .clk(clk), .clr(rst));
  Register #(.width(32)) register_12 (.D(wr_data), .en(W12), .Q(Q12), .clk(clk), .clr(rst));
  Register #(.width(32)) register_13 (.D(wr_data), .en(W13), .Q(Q13), .clk(clk), .clr(rst));
  Register #(.width(32)) register_14 (.D(wr_data), .en(W14), .Q(Q14), .clk(clk), .clr(rst));
  Register #(.width(32)) register_15 (.D(wr_data), .en(W15), .Q(Q15), .clk(clk), .clr(rst));
  // Probe on Q16
  // Probe on Q17
  // Probe on Q18
  // Probe on Q19
  // Probe on Q20
  // Probe on Q21
  // Probe on Q22
  // Probe on Q23
  // Probe on Q24
  // Probe on Q25
  // Probe on Q26
  // Probe on Q27
  // Probe on Q28
  // Probe on Q29
  // Probe on Q30
  // Probe on Q31
  Register #(.width(32)) register_16 (.D(wr_data), .en(W16), .Q(Q16), .clk(clk), .clr(rst));
  Register #(.width(32)) register_17 (.D(wr_data), .en(W17), .Q(Q17), .clk(clk), .clr(rst));
  Register #(.width(32)) register_18 (.D(wr_data), .en(W18), .Q(Q18), .clk(clk), .clr(rst));
  Register #(.width(32)) register_19 (.D(wr_data), .en(W19), .Q(Q19), .clk(clk), .clr(rst));
  Register #(.width(32)) register_20 (.D(wr_data), .en(W20), .Q(Q20), .clk(clk), .clr(rst));
  Register #(.width(32)) register_21 (.D(wr_data), .en(W21), .Q(Q21), .clk(clk), .clr(rst));
  Register #(.width(32)) register_22 (.D(wr_data), .en(W22), .Q(Q22), .clk(clk), .clr(rst));
  Register #(.width(32)) register_23 (.D(wr_data), .en(W23), .Q(Q23), .clk(clk), .clr(rst));
  Register #(.width(32)) register_24 (.D(wr_data), .en(W24), .Q(Q24), .clk(clk), .clr(rst));
  Register #(.width(32)) register_25 (.D(wr_data), .en(W25), .Q(Q25), .clk(clk), .clr(rst));
  Register #(.width(32)) register_26 (.D(wr_data), .en(W26), .Q(Q26), .clk(clk), .clr(rst));
  Register #(.width(32)) register_27 (.D(wr_data), .en(W27), .Q(Q27), .clk(clk), .clr(rst));
  Register #(.width(32)) register_28 (.D(wr_data), .en(W28), .Q(Q28), .clk(clk), .clr(rst));
  Register #(.width(32)) register_29 (.D(wr_data), .en(W29), .Q(Q29), .clk(clk), .clr(rst));
  Register #(.width(32)) register_30 (.D(wr_data), .en(W30), .Q(Q30), .clk(clk), .clr(rst));
  Register #(.width(32)) register_31 (.D(wr_data), .en(W31), .Q(Q31), .clk(clk), .clr(rst));
  Multiplexer #(.select(5), .width(32), .disabled(0), .enable("false")) multiplexer_1 (
    .in0({32{1'b0}}), .in1(Q01), .in2(Q02), .in3(Q03), .in4(Q04), .in5(Q05), .in6(Q06), .in7(Q07), .in8(Q08),
    .in9(Q09), .in10(Q10), .in11(Q11), .in12(Q12), .in13(Q13), .in14(Q14), .in15(Q15), .in16(Q16),
    .in17(Q17), .in18(Q18), .in19(Q19), .in20(Q20), .in21(Q21), .in22(Q22), .in23(Q23), .in24(Q24),
    .in25(Q25), .in26(Q26), .in27(Q27), .in28(Q28), .in29(Q29), .in30(Q30), .in31(Q31), .out(rd_data1),
    .sel(rd_reg1));
  Multiplexer #(.select(5), .width(32), .disabled(0), .enable("false")) multiplexer_2 (
    .in0({32{1'b0}}), .in1(Q01), .in2(Q02), .in3(Q03), .in4(Q04), .in5(Q05), .in6(Q06), .in7(Q07), .in8(Q08),
    .in9(Q09), .in10(Q10), .in11(Q11), .in12(Q12), .in13(Q13), .in14(Q14), .in15(Q15), .in16(Q16),
    .in17(Q17), .in18(Q18), .in19(Q19), .in20(Q20), .in21(Q21), .in22(Q22), .in23(Q23), .in24(Q24),
    .in25(Q25), .in26(Q26), .in27(Q27), .in28(Q28), .in29(Q29), .in30(Q30), .in31(Q31), .out(rd_data2),
    .sel(rd_reg2));

  // Other names for the same wires on the sheet: D[31:0] = wr_data

  // Notes on the sheet:
  //   Write Register Select
  //   Data Input
  //   Probes of all registers (for easy debugging)
  //   Read Register Select
endmodule

module ALU (
  input  [31:0] op1,
  input  [31:0] op2,
  input  [5:0] ALU_code,
  input  [5:0] ALU_code_2,
  output [31:0] result
);

  wire funct_add, funct_and, funct_or, funct_sel_en, funct_sub;
  wire [1:0] funct_sel;
  wire [31:0] multiplexer_2_out, multiplexer_3_out, multiplexer_4_out, res_add, res_and, res_or, res_sub,
       undriven;

  Adder #(.width(32)) adder_1 (.a(op1), .b(op2), .out(res_add));  // open: cin, cout
  Subtractor #(.width(32)) subtractor_1 (.a(op1), .b(op2), .out(res_sub));  // open: bin, bout
  assign res_and = op1 & op2;  // AND_Gate and_1, 32 bits wide
  assign res_or = op1 | op2;  // OR_Gate or_1, 32 bits wide
  Comparator #(.width(6)) comparator_1 (.a(ALU_code), .b(6'b100000), .eq(funct_add));  // open: gt, lt
  Comparator #(.width(6)) comparator_2 (.a(ALU_code), .b(6'b100010), .eq(funct_sub));  // open: gt, lt
  Comparator #(.width(6)) comparator_3 (.a(ALU_code), .b(6'b100100), .eq(funct_and));  // open: gt, lt
  Comparator #(.width(6)) comparator_4 (.a(ALU_code), .b(6'b100101), .eq(funct_or));  // open: gt, lt
  Priority_Encoder #(.select(2), .disabled(0)) priority_encoder_1 (
    .in0(funct_add), .in1(funct_sub), .in2(funct_and), .in3(funct_or), .out(funct_sel), .gs(funct_sel_en),
    .en_in(1'b1));  // open: en_out
  Multiplexer #(.select(2), .width(32), .disabled(0)) multiplexer_1 (
    .in0(res_add), .in1(res_sub), .in2(res_and), .in3(res_or), .out(result), .sel(funct_sel),
    .en(funct_sel_en));
  Multiplexer #(.select(5), .width(32), .disabled(0)) multiplexer_2 (
    .out(multiplexer_2_out), .sel(ALU_code_2[4:0]));  // open: in0, in1, in2, in3, in4, in5, in6, in7, in8, in9, in10, in11, in12, in13, in14, in15, in16, in17, in18, in19, in20, in21, in22, in23, in24, in25, in26, in27, in28, in29, in30, in31, en
  Multiplexer #(.select(5), .width(32), .disabled(0)) multiplexer_3 (
    .in2(undriven), .out(multiplexer_3_out), .sel(ALU_code_2[4:0]));  // open: in0, in1, in3, in4, in5, in6, in7, in8, in9, in10, in11, in12, in13, in14, in15, in16, in17, in18, in19, in20, in21, in22, in23, in24, in25, in26, in27, in28, in29, in30, in31, en
  Multiplexer #(.width(32), .disabled(0)) multiplexer_4 (
    .in0(multiplexer_2_out), .in1(multiplexer_3_out), .out(multiplexer_4_out), .sel(ALU_code_2[5]));  // open: en

  // Notes on the sheet:
  //   Results 
  //   Results Order
  //   Order must be same order as results
  //   Expand Encoder if needed
  //   Or you can try to attempt this
  //   Simply put the result in the corresponding selection
  //   ie. if opcode/func is 100010 then put result in slot 34
  //   just remember the slots start at 0.
  //   Expand MUX if needed
  //   result 34
  //   result
endmodule
